# Fritzing sketch WinchSchematic (saved by Fritzing 0.9.4)
breadboards: 1

parts:
  Arduino_Nano = Arduino Nano v2.3
  Footswitch = SWITCH-MOMENTARY-2 [package=tactile-pth-12mm]
  Max_Pot = POT [package=trim_pot]
  Min_Pot = POT [package=trim_pot]
  Dwell_Pot = POT [package=trim_pot]
  Brake_Actuator = Basic Servo
  24_to_5vdc_Converter = Voltage Regulator [package=to-92]

nets:
  N1: Arduino_Nano.D0RX, Footswitch.1
  GND: Arduino_Nano.GND, Footswitch.2, Max_Pot.A, Min_Pot.A, Dwell_Pot.A, Brake_Actuator.gnd, 24_to_5vdc_Converter.GND
  N2: Arduino_Nano.D6, Brake_Actuator.pulse
  N3: Arduino_Nano.A2, Max_Pot.S
  N4: Arduino_Nano.A1, Min_Pot.S
  N5: Arduino_Nano.A0, Dwell_Pot.S
  VIN: Arduino_Nano.VIN, Max_Pot.E, Min_Pot.E, Dwell_Pot.E, Brake_Actuator.vcc, 24_to_5vdc_Converter.OUT

notes:
  RC Model Winch Brake , Servo driven brake circuit for RC Model Electric Winch, 2.1
